# Fritzing sketch double_led (saved by Fritzing 0.9.2b)
breadboards: 1

parts:
  Part1 = Arduino 101
  R1 = Resistor [tolerance=±5% resistance=220 package=THT]
  LED1 = LED - 5mm [color="Red (633nm)" package="5 mm [THT]"]
  R2 = Resistor [tolerance=±5% resistance=220 package=THT]
  LED2 = LED - 5mm [color="Green (555nm)" package="5 mm [THT]"]

nets:
  N1: Part1.A0, LED2.cathode
  N2: Part1.D8, LED1.cathode
  N3: Part1.GND, R1.Pin_1, R2.Pin_1
  N4: R1.Pin_0, LED1.anode
  N5: R2.Pin_0, LED2.anode

custom parts:
  Arduino 101: A learning and development board that delivers the performance and low-power consumption of the Intel® Curie™ Module with the simplicity of Arduino at an entry-level price. It keeps the same robust form factor and peripheral list of the UNO with the addition of onboard Bluetooth LE capabilities and a 6-axis accelerometer/gyro to help you easily expand your creativity into the connected world.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
